# Fritzing sketch 8fragment_74HC595N (saved by Fritzing 0.9.1b)
breadboards: 1

parts:
  Raspberry_Pi1 = Raspberry Pi B rev2
  U1 = 74HC595 [package="DIP16 [THT]"]
  DI1 = 7-Segment LED Display [package=THT]
  R1 = Resistor [tolerance=±5% resistance=1k package="0603 [SMD]"]

nets:
  5V: Raspberry_Pi1.5V, U1.MR, U1.VCC
  GND: Raspberry_Pi1.GND, U1.GND, U1.OE, R1.Pin_1
  N1: Raspberry_Pi1.GPIO_17, U1.DS
  N2: Raspberry_Pi1.GPIO_18, U1.ST_CP
  N3: Raspberry_Pi1.GPIO_27, U1.SH_CP
  N4: U1.Q1, DI1.cathodeF
  N5: U1.Q2, DI1.cathodeA
  N6: U1.Q3, DI1.cathodeB
  N7: U1.Q4, DI1.cathodeE
  N8: U1.Q5, DI1.cathodeD
  N9: U1.Q6, DI1.cathodeC
  N10: U1.Q7, DI1.cathodeDP
  N11: U1.Q0, DI1.cathodeG
  N12: DI1.commAnode#2, R1.Pin_0
