# Fritzing sketch led_btn (saved by Fritzing 0.9.1b)
breadboards: 1

parts:
  Raspberry_Pi1 = Raspberry Pi B rev2
  LED1 = LED - 5mm [color="Red (633nm)" package="5 mm [THT]"]
  R1 = Resistor [tolerance=±5% resistance=220 package="1206 [SMD]"]
  S1 = Pushbutton [package="[THT]"]

nets:
  N1: Raspberry_Pi1.GND, LED1.cathode, S1.Pin_1, S1.Pin_2
  N2: Raspberry_Pi1.GPIO_17, R1.Pin_1
  N3: Raspberry_Pi1.GPIO_18, S1.Pin_3, S1.Pin_4
  N4: LED1.anode, R1.Pin_0
