# Fritzing sketch rgb_led (saved by Fritzing 0.9.1b)
breadboards: 1

parts:
  Raspberry_Pi1 = Raspberry Pi B rev2
  LED2 = RGB LED (com. cathode, rgb) [package="5 mm [THT]"]
  R1 = Resistor [tolerance=±5% resistance=220 package=THT]
  R2 = Resistor [tolerance=±5% resistance=220 package=THT]
  R3 = Resistor [tolerance=±5% resistance=220 package=THT]

nets:
  N1: Raspberry_Pi1.GND, LED2.common_cathode
  N2: Raspberry_Pi1.GPIO_17, R1.Pin_1
  N3: Raspberry_Pi1.GPIO_18, R2.Pin_1
  N4: Raspberry_Pi1.GPIO_27, R3.Pin_1
  N5: LED2.red_anode, R1.Pin_0
  N6: LED2.green_anode, R2.Pin_0
  N7: LED2.blue_anode, R3.Pin_0
